# Fritzing sketch Pokedex_circuito (saved by Fritzing 0.9.3b)

parts:
  Raspberry_Pi_3 = Raspberry Pi 3 [part_number=RPI-3-V1.2]
  Mod20 = KY-016 RGB Full Color LED Module [package="Breakout board"]

nets:
  N1: Raspberry_Pi_3.GIPO17, Mod20.R
  N2: Raspberry_Pi_3.GIPO27, Mod20.G
  N3: Raspberry_Pi_3.GIPO22, Mod20.B
  N4: Raspberry_Pi_3.GND, Mod20.-

custom parts:
  KY-016 RGB Full Color LED Module: KY-016 Arduino full color 5mm RGB LED, different colors can be obtained by mixing the three primary colors.
